// Logisim project LAB1.circ as structural Verilog: 1 circuit, main circuit main
module main (
  input  [3:0] A,
  input  [3:0] B,
  input  A_S,
  input  R_W,
  input  A_L,
  input  A_O,
  output [3:0] A_2,
  output [3:0] B_2,
  output [3:0] C
);

  wire [3:0] adder_1_out, and_1_out, multiplexer_1_out, multiplexer_2_out, multiplexer_3_out, or_1_out,
       subtractor_1_out;

  Adder #(.width(4)) adder_1 (.a(A), .b(B), .out(adder_1_out));  // open: cin, cout
  Subtractor #(.width(4)) subtractor_1 (.a(A), .b(B), .out(subtractor_1_out));  // open: bin, bout
  assign and_1_out = A & B;  // AND_Gate and_1, 4 bits wide
  assign or_1_out = A | B;  // OR_Gate or_1, 4 bits wide
  Multiplexer #(.width(4)) multiplexer_1 (
    .in0(adder_1_out), .in1(subtractor_1_out), .out(multiplexer_1_out), .sel(A_S));  // open: en
  Multiplexer #(.width(4)) multiplexer_2 (
    .in0(and_1_out), .in1(or_1_out), .out(multiplexer_2_out), .sel(A_O));  // open: en
  Multiplexer #(.width(4)) multiplexer_3 (
    .in0(multiplexer_1_out), .in1(multiplexer_2_out), .out(multiplexer_3_out), .sel(A_L));  // open: en
  Register #(.width(4)) register_1 (.D(A), .Q(A_2), .clk(R_W));  // open: en, clr
  Register #(.width(4)) register_2 (.D(B), .Q(B_2), .clk(R_W));  // open: en, clr
  Register #(.width(4)) register_3 (.D(multiplexer_3_out), .Q(C), .clk(R_W));  // open: en, clr
endmodule
